// Logisim project ECE_649_Final_Project_Sam_Green_Josh_Grimes.circ as structural Verilog: 1 circuit, main circuit main
module main (
  input  rst,
  input  in_2,
  output [31:0] out_3,
  output [31:0] out_4,
  output [31:0] out_5
);

  wire and_2_out, and_3_out, and_4_out, and_5_out, and_7_out, and_8_out, and_9_out, and_10_out, clk_out,
       comparator_1_eq, comparator_2_eq, comparator_3_eq, comparator_4_eq, comparator_5_eq, comparator_6_eq,
       comparator_7_eq, comparator_8_eq, comparator_9_eq, comparator_10_eq, comparator_11_gt, d_ff_1_qn,
       decoder_1_out1, decoder_1_out2, decoder_1_out3, decoder_1_out4, decoder_1_out5, decoder_1_out6,
       decoder_1_out7, decoder_1_out8, decoder_1_out9, decoder_1_out10, decoder_1_out11, decoder_1_out12,
       decoder_1_out13, decoder_1_out14, decoder_1_out15, decoder_2_out4, decoder_2_out8, decoder_2_out12,
       decoder_2_out24, not_1_out, not_3_out, not_4_out, not_5_out, not_6_out, not_7_out, or_1_out, or_2_out,
       or_3_out;
  wire [1:0] decoder_2_out0;
  wire [3:0] bit_extender_3_out, bit_extender_6_out, bit_extender_7_out;
  wire [7:0] adder_1_out, adder_2_out, adder_3_out, bit_extender_1_out, multiplexer_1_out, PC_q;
  wire [9:0] bit_extender_2_out, l0_q, l1_q, l2_q, l3_q, l4_q, l5_q, l6_q, l7_q, l8_q, l9_q,
       multiplexer_3_out, multiplexer_4_out, multiplexer_5_out, multiplexer_6_out, multiplexer_7_out,
       multiplexer_8_out, multiplexer_9_out, multiplexer_10_out, multiplexer_11_out, multiplexer_12_out;
  wire [23:0] adder_3_out_2;
  wire [31:0] adder_4_out, adder_5_out, and_1_out, bit_extender_4_out, bit_extender_5_out, DataMem_dout,
       InMEM_dout, multiplexer_2_out, multiplexer_13_out, multiplexer_15_out, multiplexer_16_out,
       multiplexer_19_out, not_2_out, x0_q, x1_q, x2_q, x3_q, x4_q, x5_q, x6_q, x7_q, x8_q, x9_q, x10_q,
       x11_q, x12_q, x13_q, x14_q, x15_q, xor_1_out;

  Clock clk (.out(clk_out));
  Register PC (.D(multiplexer_1_out), .en(1'b1), .clk(clk_out), .Q(PC_q), .clr(rst));
  Bit_Extender #(.in_width(13), .out_width(8), .\type ("zero")) bit_extender_1 (
    .in({InMEM_dout[31], InMEM_dout[7], InMEM_dout[30:25], InMEM_dout[11:8], 1'b0}), .out(bit_extender_1_out));
  Adder adder_1 (.a(bit_extender_1_out), .b(PC_q), .out(adder_1_out));  // open: cin, cout
  Adder adder_2 (.a(8'h1), .b(PC_q), .out(adder_2_out));  // open: cin, cout
  RAM #(.dataWidth(32)) InMEM (.addr(PC_q), .we(1'b0), .oe(1'b1), .clk(clk_out), .dout(InMEM_dout));  // open: din
  RAM #(.dataWidth(32)) DataMem (
    .addr(adder_3_out), .we(decoder_2_out8), .oe(1'b1), .clk(clk_out), .din(multiplexer_15_out),
    .dout(DataMem_dout));
  Multiplexer #(.width(8)) multiplexer_1 (
    .in0(adder_2_out), .in1(adder_1_out), .out(multiplexer_1_out), .sel(or_1_out));
  Adder #(.width(32)) adder_3 (
    .a(multiplexer_13_out), .b(multiplexer_2_out), .out({adder_3_out_2, adder_3_out}));  // open: cin, cout
  Multiplexer #(.width(32)) multiplexer_2 (
    .in0(bit_extender_5_out), .in1(bit_extender_4_out), .out(multiplexer_2_out), .sel(decoder_2_out0[0]));
  Bit_Extender #(.in_width(32), .out_width(10)) bit_extender_2 (.in(multiplexer_15_out), .out(bit_extender_2_out));
  Bit_Extender #(.in_width(5), .out_width(4), .\type ("zero")) bit_extender_3 (
    .in(InMEM_dout[11:7]), .out(bit_extender_3_out));
  assign bit_extender_4_out = {{20{InMEM_dout[31]}}, InMEM_dout[31:20]};  // Bit_Extender bit_extender_4
  Comparator comparator_1 (.a(adder_3_out), .b(8'h50), .eq(comparator_1_eq));  // open: gt, lt
  Comparator comparator_2 (.a(adder_3_out), .b(8'h54), .eq(comparator_2_eq));  // open: gt, lt
  Comparator comparator_3 (.a(adder_3_out), .b(8'h58), .eq(comparator_3_eq));  // open: gt, lt
  Comparator comparator_4 (.a(adder_3_out), .b(8'h5c), .eq(comparator_4_eq));  // open: gt, lt
  Comparator comparator_5 (.a(adder_3_out), .b(8'h60), .eq(comparator_5_eq));  // open: gt, lt
  Comparator comparator_6 (.a(adder_3_out), .b(8'h64), .eq(comparator_6_eq));  // open: gt, lt
  Comparator comparator_7 (.a(adder_3_out), .b(8'h68), .eq(comparator_7_eq));  // open: gt, lt
  Comparator comparator_8 (.a(adder_3_out), .b(8'h6c), .eq(comparator_8_eq));  // open: gt, lt
  Comparator comparator_9 (.a(adder_3_out), .b(8'h70), .eq(comparator_9_eq));  // open: gt, lt
  Comparator comparator_10 (.a(adder_3_out), .b(8'h74), .eq(comparator_10_eq));  // open: gt, lt
  Decoder #(.select(4)) decoder_1 (
    .out1(decoder_1_out1), .out2(decoder_1_out2), .out3(decoder_1_out3), .out4(decoder_1_out4),
    .out5(decoder_1_out5), .out6(decoder_1_out6), .out7(decoder_1_out7), .out8(decoder_1_out8),
    .out9(decoder_1_out9), .out10(decoder_1_out10), .out11(decoder_1_out11), .out12(decoder_1_out12),
    .out13(decoder_1_out13), .out14(decoder_1_out14), .out15(decoder_1_out15), .sel(bit_extender_3_out),
    .en(and_9_out));  // open: out0
  assign bit_extender_5_out = {{20{InMEM_dout[31]}}, {InMEM_dout[31:25], InMEM_dout[11:7]}};  // Bit_Extender bit_extender_5
  Register #(.width(10)) l0 (.D(bit_extender_2_out), .en(comparator_1_eq), .clk(clk_out), .Q(l0_q), .clr(rst));
  Register #(.width(10)) l1 (.D(bit_extender_2_out), .en(comparator_2_eq), .clk(clk_out), .Q(l1_q), .clr(rst));
  Register #(.width(10)) l2 (.D(bit_extender_2_out), .en(comparator_3_eq), .clk(clk_out), .Q(l2_q), .clr(rst));
  Register #(.width(10)) l3 (.D(bit_extender_2_out), .en(comparator_4_eq), .clk(clk_out), .Q(l3_q), .clr(rst));
  Register #(.width(10)) l4 (.D(bit_extender_2_out), .en(comparator_5_eq), .clk(clk_out), .Q(l4_q), .clr(rst));
  Register #(.width(10)) l5 (.D(bit_extender_2_out), .en(comparator_6_eq), .clk(clk_out), .Q(l5_q), .clr(rst));
  Register #(.width(10)) l6 (.D(bit_extender_2_out), .en(comparator_7_eq), .clk(clk_out), .Q(l6_q), .clr(rst));
  Register #(.width(10)) l7 (.D(bit_extender_2_out), .en(comparator_8_eq), .clk(clk_out), .Q(l7_q), .clr(rst));
  Register #(.width(10)) l8 (.D(bit_extender_2_out), .en(comparator_9_eq), .clk(clk_out), .Q(l8_q), .clr(rst));
  Register #(.width(10)) l9 (.D(bit_extender_2_out), .en(comparator_10_eq), .clk(clk_out), .Q(l9_q), .clr(rst));
  Bit_Extender #(.in_width(5), .out_width(4), .\type ("zero")) bit_extender_6 (
    .in(InMEM_dout[19:15]), .out(bit_extender_6_out));
  Bit_Extender #(.in_width(5), .out_width(4), .\type ("zero")) bit_extender_7 (
    .in(InMEM_dout[24:20]), .out(bit_extender_7_out));
  Multiplexer #(.width(10)) multiplexer_3 (.in0({10{1'b0}}), .in1(l0_q), .out(multiplexer_3_out), .sel(in_2));
  Multiplexer #(.width(10)) multiplexer_4 (.in0(10'h18), .in1(l1_q), .out(multiplexer_4_out), .sel(in_2));
  Multiplexer #(.width(10)) multiplexer_5 (.in0(10'h4), .in1(l2_q), .out(multiplexer_5_out), .sel(in_2));
  Multiplexer #(.width(10)) multiplexer_6 (.in0(10'h1c2), .in1(l3_q), .out(multiplexer_6_out), .sel(in_2));
  Multiplexer #(.width(10)) multiplexer_7 (.in0(10'h2), .in1(l4_q), .out(multiplexer_7_out), .sel(in_2));
  Multiplexer #(.width(10)) multiplexer_8 (.in0(10'h2), .in1(l5_q), .out(multiplexer_8_out), .sel(in_2));
  Multiplexer #(.width(10)) multiplexer_9 (.in0(10'h1c2), .in1(l6_q), .out(multiplexer_9_out), .sel(in_2));
  Multiplexer #(.width(10)) multiplexer_10 (.in0(10'h4), .in1(l7_q), .out(multiplexer_10_out), .sel(in_2));
  Multiplexer #(.width(10)) multiplexer_11 (.in0(10'h18), .in1(l8_q), .out(multiplexer_11_out), .sel(in_2));
  Multiplexer #(.width(10)) multiplexer_12 (.in0({10{1'b0}}), .in1(l9_q), .out(multiplexer_12_out), .sel(in_2));
  Register #(.width(32)) x0 (.D(out_5), .en(1'b0), .clk(clk_out), .Q(x0_q), .clr(rst));
  Register #(.width(32)) x1 (.D(out_5), .en(decoder_1_out1), .clk(clk_out), .Q(x1_q), .clr(rst));
  Register #(.width(32)) x2 (.D(out_5), .en(decoder_1_out2), .clk(clk_out), .Q(x2_q), .clr(rst));
  Register #(.width(32)) x3 (.D(out_5), .en(decoder_1_out3), .clk(clk_out), .Q(x3_q), .clr(rst));
  Register #(.width(32)) x4 (.D(out_5), .en(decoder_1_out4), .clk(clk_out), .Q(x4_q), .clr(rst));
  Register #(.width(32)) x5 (.D(out_5), .en(decoder_1_out5), .clk(clk_out), .Q(x5_q), .clr(rst));
  Register #(.width(32)) x6 (.D(out_5), .en(decoder_1_out6), .clk(clk_out), .Q(x6_q), .clr(rst));
  Register #(.width(32)) x7 (.D(out_5), .en(decoder_1_out7), .clk(clk_out), .Q(x7_q), .clr(rst));
  DotMatrix #(.matrixcols(10), .matrixrows(10)) dotmatrix_1 (
    .col0(multiplexer_3_out), .col1(multiplexer_4_out), .col2(multiplexer_5_out), .col3(multiplexer_6_out),
    .col4(multiplexer_7_out), .col5(multiplexer_8_out), .col6(multiplexer_9_out), .col7(multiplexer_10_out),
    .col8(multiplexer_11_out), .col9(multiplexer_12_out));
  Register #(.width(32)) x8 (.D(out_5), .en(decoder_1_out8), .clk(clk_out), .Q(x8_q), .clr(rst));
  Register #(.width(32)) x9 (.D(out_5), .en(decoder_1_out9), .clk(clk_out), .Q(x9_q), .clr(rst));
  Register #(.width(32)) x10 (.D(out_5), .en(decoder_1_out10), .clk(clk_out), .Q(x10_q), .clr(rst));
  Register #(.width(32)) x11 (.D(out_5), .en(decoder_1_out11), .clk(clk_out), .Q(x11_q), .clr(rst));
  Register #(.width(32)) x12 (.D(out_5), .en(decoder_1_out12), .clk(clk_out), .Q(x12_q), .clr(rst));
  Register #(.width(32)) x13 (.D(out_5), .en(decoder_1_out13), .clk(clk_out), .Q(x13_q), .clr(rst));
  Register #(.width(32)) x14 (.D(out_5), .en(decoder_1_out14), .clk(clk_out), .Q(x14_q), .clr(rst));
  Register #(.width(32)) x15 (.D(out_5), .en(decoder_1_out15), .clk(clk_out), .Q(x15_q), .clr(rst));
  D_Flip_Flop d_ff_1 (.D(InMEM_dout[13]), .clk(clk_out), .Qn(d_ff_1_qn));  // open: Q, preset, reset
  Multiplexer #(.select(4), .width(32)) multiplexer_13 (
    .in0(x0_q), .in1(x1_q), .in2(x2_q), .in3(x3_q), .in4(x4_q), .in5(x5_q), .in6(x6_q), .in7(x7_q),
    .in8(x8_q), .in9(x9_q), .in10(x10_q), .in11(x11_q), .in12(x12_q), .in13(x13_q), .in14(x14_q),
    .in15(x15_q), .out(multiplexer_13_out), .sel(bit_extender_6_out));
  assign and_1_out = multiplexer_15_out & multiplexer_13_out;  // AND_Gate and_1, 32 bits wide
  Multiplexer #(.width(32)) multiplexer_14 (.in1(and_1_out), .out(out_3), .sel(decoder_2_out0[1]));  // open: in0
  Multiplexer #(.select(4), .width(32)) multiplexer_15 (
    .in0(x0_q), .in1(x1_q), .in2(x2_q), .in3(x3_q), .in4(x4_q), .in5(x5_q), .in6(x6_q), .in7(x7_q),
    .in8(x8_q), .in9(x9_q), .in10(x10_q), .in11(x11_q), .in12(x12_q), .in13(x13_q), .in14(x14_q),
    .in15(x15_q), .out(multiplexer_15_out), .sel(bit_extender_7_out));
  or or_1 (or_1_out, and_8_out, and_5_out);
  Adder #(.width(32)) adder_4 (.a(multiplexer_13_out), .b(multiplexer_16_out), .out(adder_4_out));  // open: cin, cout
  and and_2 (and_2_out, d_ff_1_qn, decoder_2_out4);
  Multiplexer #(.width(32)) multiplexer_16 (
    .in0(multiplexer_19_out), .in1(adder_5_out), .out(multiplexer_16_out), .sel(or_2_out));
  Adder #(.width(32)) adder_5 (.a(not_2_out), .b(32'h1), .out(adder_5_out));  // open: cin, cout
  or or_2 (or_2_out, and_3_out, decoder_2_out24);
  and and_3 (and_3_out, InMEM_dout[30], and_4_out);
  and and_4 (and_4_out, decoder_2_out12, not_3_out);
  Multiplexer #(.select(2), .width(32)) multiplexer_17 (
    .in0(out_4), .in1(DataMem_dout), .in2(out_3), .out(out_5), .sel(decoder_2_out0));  // open: in3
  and and_5 (and_5_out, decoder_2_out24, InMEM_dout[12], not_1_out);
  not not_1 (not_1_out, and_10_out);
  Multiplexer #(.width(32)) multiplexer_18 (.in0(adder_4_out), .in1(xor_1_out), .out(out_4), .sel(and_2_out));
  assign not_2_out = ~multiplexer_19_out;  // NOT_Gate not_2, 32 bits wide
  and and_6 (decoder_2_out0[1], decoder_2_out12, and_7_out);
  or or_3 (or_3_out, InMEM_dout[12], InMEM_dout[13], InMEM_dout[14]);
  not not_3 (not_3_out, or_3_out);
  and and_7 (and_7_out, InMEM_dout[12], InMEM_dout[13], InMEM_dout[14]);
  assign xor_1_out = multiplexer_13_out ^ multiplexer_16_out;  // XOR_Gate xor_1, 32 bits wide
  Multiplexer #(.width(32)) multiplexer_19 (
    .in0(multiplexer_15_out), .in1(bit_extender_4_out), .out(multiplexer_19_out), .sel(decoder_2_out4));
  and and_8 (and_8_out, decoder_2_out24, not_4_out, and_10_out);
  not not_4 (not_4_out, InMEM_dout[12]);
  not not_5 (not_5_out, decoder_2_out8);
  LED led_1 (.in(decoder_2_out0[0]));
  LED led_2 (.in(decoder_2_out4));
  LED led_3 (.in(decoder_2_out8));
  LED led_4 (.in(decoder_2_out12));
  LED led_5 (.in(decoder_2_out24));
  and and_9 (and_9_out, not_5_out, not_6_out);
  not not_6 (not_6_out, decoder_2_out24);
  Decoder #(.select(5)) decoder_2 (
    .out0(decoder_2_out0[0]), .out4(decoder_2_out4), .out8(decoder_2_out8), .out12(decoder_2_out12),
    .out24(decoder_2_out24), .sel(InMEM_dout[6:2]), .en(1'b1));  // open: out1, out2, out3, out5, out6, out7, out9, out10, out11, out13, out14, out15, out16, out17, out18, out19, out20, out21, out22, out23, out25, out26, out27, out28, out29, out30, out31
  Comparator #(.mode("unsigned"), .width(32)) comparator_11 (
    .a(out_4), .b({32{1'b0}}), .gt(comparator_11_gt));  // open: eq, lt
  not not_7 (not_7_out, comparator_11_gt);
  and and_10 (and_10_out, not_7_out, 1'b1);

  // Notes on the sheet:
  //   pc_offset
  //   memory for lw, sw
  //   1: branch; 0: no-branch
  //   instructions stored in this ram
  //   fun7
  //   offset 10:5
  //   offset 12
  //   opcode
  //   rd
  //   fun3
  //   rs2
  //   offset[4-0]
  //   offset[11-5]
  //   offset 11
  //   rs1
  //   Imm
  //   offset 4:1
  //   write_reg
  //   the three 5 -> 4 extenders could be wrong
  //   data_rs2
  //   write_data
  //   toggle auto-generation of the smiley face (should be toggled high when testing)
  //   16 registers
  //   clk_sig
  //   rst_sig
  //   led matrix for smiley face
  //   fun3; 14-12
  //   and
  //   add/sub
  //   MUX to control write data of the registers
  //   register decoder set
  //   Control
  //   lw
  //   addi/xori
  //   sw
  //   add/sub/and
  //   beq/bne
endmodule
